# Fritzing sketch Untitled Sketch 2 (saved by Fritzing 0.9.5d)

parts:
  Gizwits_WiFi_Witty_ESP-12F1 = Gizwits WiFi Witty ESP-12F
  Part1 = Motor Driver 1A Dual TB6612FNG
  U1 = LIPO-1000mAh [package=lipo-1000]
  M1 = DC Motor
  M2 = DC Motor

nets:
  N1: Gizwits_WiFi_Witty_ESP-12F1.GPIO14, Part1.PWMA
  N2: Gizwits_WiFi_Witty_ESP-12F1.GPIO12, Part1.BIN1
  N3: Gizwits_WiFi_Witty_ESP-12F1.GPIO13, Part1.BIN2
  N4: Gizwits_WiFi_Witty_ESP-12F1.VCC, Part1.STBY
  GND: Gizwits_WiFi_Witty_ESP-12F1.GND, Part1.GND, U1.-
  N5: Gizwits_WiFi_Witty_ESP-12F1.GPIO15, Part1.PWMB
  N6: Gizwits_WiFi_Witty_ESP-12F1.GPIO4, Part1.AIN1
  N7: Gizwits_WiFi_Witty_ESP-12F1.GPIO5, Part1.AIN2
  N8: Part1.B01, M2.pin_2
  N9: Part1.B02, M2.pin_1
  N10: Part1.A02, M1.pin_2
  N11: Part1.A01, M1.pin_1
  N12: Part1.VM, U1.+
